// Logisim project ALU.circ as structural Verilog: 1 circuit, main circuit main
module main (
  input  [3:0] A,
  input  [3:0] B,
  input  [2:0] in_3
);

  wire nor_1_out;
  wire [3:0] adder_1_out, and_1_out, multiplexer_7_out, multiplexer_8_out, multiplexer_9_out, not_1_out,
       xor_1_out;

  Adder #(.width(4)) adder_1 (.a(A), .b(and_1_out), .out(adder_1_out), .cin(in_3[0]));  // open: cout
  Multiplexer #(.select(2)) multiplexer_1 (
    .in0(adder_1_out[3]), .in1(adder_1_out[3]), .in2(A[3]), .in3(adder_1_out[3]), .out(multiplexer_8_out[3]),
    .sel(in_3[1:0]));  // open: en
  Multiplexer #(.select(2)) multiplexer_2 (
    .in0(1'b0), .in1(A[3]), .in2(A[2]), .in3(A[1]), .out(multiplexer_7_out[3]), .sel(in_3[1:0]));  // open: en
  Multiplexer #(.select(2)) multiplexer_3 (
    .in0(A[3]), .in1(A[3]), .in2(A[1]), .in3(A[0]), .out(multiplexer_7_out[2]), .sel(in_3[1:0]));  // open: en
  assign and_1_out = xor_1_out & not_1_out;  // AND_Gate and_1, 4 bits wide
  Multiplexer #(.select(2)) multiplexer_4 (
    .in0(adder_1_out[2]), .in1(adder_1_out[2]), .in2(A[2]), .in3(adder_1_out[2]), .out(multiplexer_8_out[2]),
    .sel(in_3[1:0]));  // open: en
  // Probe on multiplexer_7_out
  assign not_1_out = ~{4{in_3[1]}};  // NOT_Gate not_1, 4 bits wide
  Multiplexer #(.select(2)) multiplexer_5 (
    .in0(adder_1_out[1]), .in1(adder_1_out[1]), .in2(A[1]), .in3(adder_1_out[1]), .out(multiplexer_8_out[1]),
    .sel(in_3[1:0]));  // open: en
  // Probe on multiplexer_8_out
  Multiplexer #(.select(2)) multiplexer_6 (
    .in0(A[2]), .in1(A[3]), .in2(A[0]), .in3(1'b0), .out(multiplexer_7_out[1]), .sel(in_3[1:0]));  // open: en
  assign xor_1_out = B ^ {4{in_3[0]}};  // XOR_Gate xor_1, 4 bits wide
  Multiplexer #(.select(2)) multiplexer_7 (
    .in0(A[1]), .in1(A[2]), .in2(1'b0), .in3(1'b0), .out(multiplexer_7_out[0]), .sel(in_3[1:0]));  // open: en
  Multiplexer #(.select(2)) multiplexer_8 (
    .in0(adder_1_out[0]), .in1(adder_1_out[0]), .in2(A[0]), .in3(adder_1_out[0]), .out(multiplexer_8_out[0]),
    .sel(in_3[1:0]));  // open: en
  Multiplexer #(.width(4)) multiplexer_9 (
    .in0(multiplexer_8_out), .in1(multiplexer_7_out), .out(multiplexer_9_out), .sel(in_3[2]));  // open: en
  // Probe on nor_1_out
  nor nor_1 (nor_1_out, multiplexer_9_out[3], multiplexer_9_out[2], multiplexer_9_out[1], multiplexer_9_out[0]);
  // Probe on multiplexer_9_out

  // Notes on the sheet:
  //   ALUOP
endmodule
